# Fritzing sketch Bluetooth Home Automation (saved by Fritzing 0.9.3b)
breadboards: 1

parts:
  U1 = 4-Channel 5v Relay Shield [package=relay-4ch5v10a]
  Part1 = Bluetooth HC-05 Macho  # not connected
  Part2 = Arduino Uno (Rev3)

nets:
  VCC: U1.VCC, Part2.5V
  GND: U1.GND, Part2.GND
  N1: U1.IN1, Part2.D6_PWM
  N2: U1.IN2, Part2.D5_PWM
  N3: U1.IN4, Part2.D3_PWM
  N4: U1.IN3, Part2.D4

notes:
  RAOATECH IT-ELECTROMECH
  Robotics Training

custom parts:
  4-Channel 5v Relay Shield: 4 Channel 5v Relay Shield w. 2x SPD-06VDC-SD-C
